# Fritzing sketch sximatiko (saved by Fritzing 1.0.2b)

parts:
  A1 = Seeed grove mcp9808 temp sensor
  Part1 = Arduino Uno (Rev3)
  IC1 = Rasberry Pi NIOR Camera [chip_label=IC package="DIP (Dual Inline) [THT]"]  # not connected
  part = Raspberry Pi Zero  # not connected
  Raspberry_Pi_1 = Raspberry Pi 3 [part_number=RPI-3-V1.2]  # not connected

nets:
  N1: A1.Pin_1, Part1.GND
  N2: A1.Pin_2, Part1.5V
  N3: A1.Pin_3, Part1.A4/SDA
  N4: A1.Pin_4, Part1.A5/SCL

notes:
  Camera
  CPU

custom parts:
  Seeed grove mcp9808 temp sensor: The Grove - I2C High Accuracy Temperature Sensor(MCP9808) is a high accuracy digital module based on MCP9808.
  Rasberry Pi NIOR Camera: Camera
